# Fritzing sketch z-meter_ABB_B23_circuit (saved by Fritzing 0.9.3b)
breadboards: 1

parts:
  Z-uno_2_1 = Z-Uno 2.0
  S1 = Momentary Switch [package=ksa_sealed_tac_switch]
  R1 = Resistor [tolerance=±5% resistance=10k package=THT]
  LED1 = LED - 5mm [color="Red (633nm)" package="5 mm [THT]"]
  R2 = Resistor [tolerance=±5% resistance=1k package=THT]
  Grove1 = Grove OLED 128x96

nets:
  N1: Z-uno_2_1.GND#3, R1.Pin_1, R2.Pin_0
  N2: Z-uno_2_1.pin6, S1.4, R1.Pin_0
  N3: Z-uno_2_1.ANT_U.FL, Z-uno_2_1.pin9, Grove1.SCL
  N4: Z-uno_2_1.pin10, Grove1.SDA
  N5: Z-uno_2_1.pin16, LED1.anode
  N6: Z-uno_2_1.pin_22, Z-uno_2_1.3V3#44
  N7: Z-uno_2_1.pin_23, Z-uno_2_1.GND#43
  N8: S1.1, Grove1.VCC
  N9: LED1.cathode, R2.Pin_1

custom parts:
  Z-Uno 2.0: The Teensy is a complete USB-based microcontoller development system, in a very small footprint, capable of implementing many types of projects. All programming is done via the USB port. No special programmer is needed, only a standard micro-USB cable and a PC or Macintosh with a USB port. It has a USB keyboard/mouse/joystick emulation stack and can be programmed through Arduino IDE. Z-Uno is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
